# Fritzing sketch DASS01_CV_AMP (saved by Fritzing 0.9.3b)
breadboards: 1

parts:
  IC1 = Dual Op-Amp [package=dip08]
  C1 = Ceramic Capacitor [capacitance=100nF package="100 mil [THT, multilayer]"]
  C2 = Ceramic Capacitor [capacitance=100nF package="100 mil [THT, multilayer]"]
  R1 = Resistor [tolerance=±5% resistance=10k package=THT]
  R2 = Resistor [tolerance=±5% resistance=20k package=THT]
  R3 = Resistor [tolerance=±5% resistance=47 package=THT]
  R4 = Rotary Potentiometer (Small) [maximum_resistance=100kΩ package=THT]
  R5 = Resistor [tolerance=±5% resistance=47 package=THT]
  R6 = Resistor [tolerance=±5% resistance=20k package=THT]
  R7 = Resistor [tolerance=±5% resistance=10k package=THT]
  R8 = Rotary Potentiometer (Small) [maximum_resistance=100kΩ package=THT]
  C3 = Electrolytic Capacitor [capacitance=1µF package="100 mil [THT, electrolytic]"]
  C4 = Electrolytic Capacitor [capacitance=1µF package="100 mil [THT, electrolytic]"]

nets:
  N1: IC1.A_OUT, R2.Pin_0, R3.Pin_0
  N2: IC1.A_-IN, R1.Pin_0, R2.Pin_1
  N3: IC1.A_+IN, R4.wiper
  N4: IC1.A_V-, C2.0, C4.-
  N5: IC1.B_-IN, R6.Pin_1, R7.Pin_1
  N6: IC1.B_OUT, R5.Pin_0, R6.Pin_0
  N7: IC1.A_V+, C1.0, C3.+
  N8: C1.1, C2.1, R1.Pin_1, R4.leg1, R7.Pin_0, R8.leg1, C3.-, C4.+

notes:
  -9V
  GND
  GND
  +9V
  To
  Antilog-MM
  MOD1
  CV Cutoff
  To
  Dual-OTA-VCA
  ENV
  CV
  Envelope
