# Fritzing sketch +5V_CommonModeChoke (saved by Fritzing 0.9.3b)
breadboards: 1

parts:
  R1 = Resistor [tolerance=±5% resistance=47 package=THT]
  C1 = Electrolytic Capacitor [capacitance=1µF package="100 mil [THT, electrolytic]"]
  U5 = mystery part, 12 pins [chip_label=choke]
  R2 = Resistor [tolerance=±5% resistance=1k package=THT]
  LED1 = LED - 5mm [color="Green (570nm)" package="5 mm [THT]"]

nets:
  N1: R1.Pin_0, C1.-, U5.pin7, U5.pin8, R2.Pin_0
  N2: R1.Pin_1, C1.+, U5.pin11, U5.pin12, LED1.anode
  N3: U5.pin1, U5.pin2
  N4: U5.pin5, U5.pin6
  N5: R2.Pin_1, LED1.cathode

notes:
  +5V
  GND
  load 47 ohm
  5V / 47ohm = 106mA
  5V x 5V / 47 ohm = 532mW
