# Fritzing sketch ±12VPSU (saved by Fritzing 0.9.3b)
breadboards: 2

parts:
  U1 = Voltage Regulator - 5V [package="DPak [SMD]"]
  U2 = Voltage Regulator - 5V [package="TO220 [THT]"]
  D1 = Rectifier Diode [part_number=1N4001 package="300 mil [THT]"]
  C1 = Ceramic Capacitor [capacitance=100nF package="100 mil [THT, multilayer]"]
  C2 = Ceramic Capacitor [capacitance=100nF package="100 mil [THT, multilayer]"]
  C3 = Electrolytic Capacitor [capacitance=1µF package="100 mil [THT, electrolytic]"]
  D2 = Rectifier Diode [part_number=1N4001 package="300 mil [THT]"]
  LED1 = LED - 5mm [color="Red (633nm)" package="5 mm [THT]"]
  R1 = Resistor [tolerance=±5% resistance=4.7k package=THT]
  C4 = Electrolytic Capacitor [capacitance=1µF package="100 mil [THT, electrolytic]"]
  C5 = Ceramic Capacitor [capacitance=100nF package="100 mil [THT, multilayer]"]
  C6 = Ceramic Capacitor [capacitance=100nF package="100 mil [THT, multilayer]"]
  D3 = Rectifier Diode [part_number=1N4001 package="300 mil [THT]"]
  D4 = Rectifier Diode [part_number=1N4001 package="300 mil [THT]"]
  R2 = Resistor [tolerance=±5% resistance=4.7k package=THT]
  LED2 = LED - 5mm [color="Blue (525nm)" package="5 mm [THT]"]
  R5 = Resistor [tolerance=±5% resistance=220 package=THT]
  R6 = Resistor [tolerance=±5% resistance=220 package=THT]

nets:
  N1: U1.input_voltage, D1.cathode, C1.1
  N2: U1.GND, U2.input_voltage, C1.0, C2.1, C3.-, D2.anode, R1.Pin_1, C4.+, C5.0, C6.1, D4.cathode, R2.Pin_0, R5.Pin_1, R6.Pin_0
  N3: U1.output_voltage, D1.anode, C2.0, C3.+, D2.cathode, LED1.anode, R5.Pin_0
  N4: U2.GND, C5.1, D3.anode
  N5: U2.output_voltage, C4.-, C6.0, D3.cathode, D4.anode, LED2.cathode, R6.Pin_1
  N6: LED1.cathode, R1.Pin_0
  N7: R2.Pin_1, LED2.anode

notes:
  7812
  1 INPUT
  2 GND
  3 OUTPUT
  GND
  +15V
  -15V
  GND
  7912
  1 COMMON
  2 IN
  3 OUT
  GND
  +12V
  -12V
  GND
  -15VIN
  +15VIN
  GNDIN
  Load 220 ohm
  12V / 220 ohm = 55mA
  12v x 12v / 220 ohm = 655mW
